// Logisim project 3.circ as structural Verilog: 10 circuits, main circuit mod60计数器
module \mod60计数器  (
  input  CLR,
  input  ADJ,
  input  CPU,
  input  CPD,
  output out_5,
  output Q2A,
  output Q2B,
  output Q2C,
  output Q2D,
  output Q1A,
  output Q1B,
  output Q1C,
  output Q1D
);

  wire and_1_out, and_2_out, and_3_out, or_1_out, \四位二进制可逆计数器_1_out_8 , \四位二进制可逆计数器_1_out_9 ;
  wire [7:0] \四位二进制可逆计数器_1_q1 ;
  wire [7:4] divider_1_out, divider_1_rem;

  or or_1 (or_1_out, out_5, CLR);
  and and_1 (and_1_out, ADJ, CPD);
  \四位二进制可逆计数器  \u_四位二进制可逆计数器_1  (
    .CLR(or_1_out), .CPU(CPU), .CPD(and_1_out), .Q1(\四位二进制可逆计数器_1_q1 [0]), .Q2(\四位二进制可逆计数器_1_q1 [1]),
    .Q3(\四位二进制可逆计数器_1_q1 [2]), .Q4(\四位二进制可逆计数器_1_q1 [3]), .out_8(\四位二进制可逆计数器_1_out_8 ),
    .out_9(\四位二进制可逆计数器_1_out_9 ));
  \四位二进制可逆计数器  \u_四位二进制可逆计数器_2  (
    .CLR(or_1_out), .CPU(\四位二进制可逆计数器_1_out_8 ), .CPD(\四位二进制可逆计数器_1_out_9 ), .Q1(\四位二进制可逆计数器_1_q1 [4]),
    .Q2(\四位二进制可逆计数器_1_q1 [5]), .Q3(\四位二进制可逆计数器_1_q1 [6]), .Q4(\四位二进制可逆计数器_1_q1 [7]));  // open: out_8, out_9
  and and_2 (and_2_out, \四位二进制可逆计数器_1_q1 [3], \四位二进制可逆计数器_1_q1 [2], \四位二进制可逆计数器_1_q1 [1], \四位二进制可逆计数器_1_q1 [0], \四位二进制可逆计数器_1_q1 [7], \四位二进制可逆计数器_1_q1 [6], \四位二进制可逆计数器_1_q1 [5], \四位二进制可逆计数器_1_q1 [4]);
  and and_3 (and_3_out, \四位二进制可逆计数器_1_q1 [3], \四位二进制可逆计数器_1_q1 [2], ~\四位二进制可逆计数器_1_q1 [1], ~\四位二进制可逆计数器_1_q1 [0], ~\四位二进制可逆计数器_1_q1 [7], ~\四位二进制可逆计数器_1_q1 [6], \四位二进制可逆计数器_1_q1 [5], \四位二进制可逆计数器_1_q1 [4]);  // AND_Gate
  or or_2 (out_5, and_2_out, and_3_out);
  Divider divider_1 (
    .a(\四位二进制可逆计数器_1_q1 ), .b(8'ha), .out({divider_1_out, Q2D, Q2C, Q2B, Q2A}),
    .rem({divider_1_rem, Q1D, Q1C, Q1B, Q1A}));  // open: upper
endmodule

module \mod12_24计数器  (
  input  CPU,
  input  ADJ,
  input  CPD,
  input  CLR,
  input  SET,
  output out_6,
  output out_7,
  output out_8,
  output out_9,
  output out_10,
  output out_11,
  output out_12,
  output out_13,
  output out_14
);

  wire and_1_out, comparator_1_lt, or_1_out, t_ff_1_q;
  wire [3:0] adder_2_out, multiplexer_2_out, subtractor_1_out;
  wire [7:0] adder_1_out, \mod60计数器_1_q1a , multiplexer_3_out;
  wire [7:4] multiplexer_1_out;

  and and_1 (and_1_out, ADJ, CPD);
  \mod60计数器  \mod60计数器_1  (
    .ADJ(1'b1), .CPU(CPU), .CPD(and_1_out), .Q1D(\mod60计数器_1_q1a [3]), .Q1C(\mod60计数器_1_q1a [2]),
    .Q1B(\mod60计数器_1_q1a [1]), .Q1A(\mod60计数器_1_q1a [0]), .Q2D(\mod60计数器_1_q1a [7]),
    .Q2C(\mod60计数器_1_q1a [6]), .Q2B(\mod60计数器_1_q1a [5]), .Q2A(\mod60计数器_1_q1a [4]), .CLR(or_1_out));  // open: out_5
  and and_2 (out_12, ~\mod60计数器_1_q1a [7], ~\mod60计数器_1_q1a [6], ~\mod60计数器_1_q1a [5], \mod60计数器_1_q1a [4], ~\mod60计数器_1_q1a [3], ~\mod60计数器_1_q1a [2], \mod60计数器_1_q1a [1], ~\mod60计数器_1_q1a [0]);  // AND_Gate
  or or_1 (or_1_out, out_12, CLR);
  Adder adder_1 (.a(\mod60计数器_1_q1a ), .b(8'h12), .out(adder_1_out));  // open: cin, cout
  Comparator #(.width(4), .mode("unsigned")) comparator_1 (
    .a(4'b1001), .b(adder_1_out[3:0]), .lt(comparator_1_lt));  // open: gt, eq
  Adder #(.width(4)) adder_2 (.a(adder_1_out[7:4]), .b(4'b0001), .out(adder_2_out));  // open: cin, cout
  Multiplexer #(.width(4), .enable("false")) multiplexer_1 (
    .in0(adder_1_out[7:4]), .in1(adder_2_out), .out(multiplexer_1_out), .sel(comparator_1_lt));
  Subtractor #(.width(4)) subtractor_1 (.a(adder_1_out[3:0]), .b(4'b1010), .out(subtractor_1_out));  // open: bin, bout
  Multiplexer #(.width(4), .enable("false")) multiplexer_2 (
    .in0(adder_1_out[3:0]), .in1(subtractor_1_out), .out(multiplexer_2_out), .sel(comparator_1_lt));
  Multiplexer #(.width(8), .enable("false")) multiplexer_3 (
    .in0(\mod60计数器_1_q1a ), .in1({multiplexer_1_out, multiplexer_2_out}), .out(multiplexer_3_out),
    .sel(t_ff_1_q));
  T_Flip_Flop #(.trigger("falling")) t_ff_1 (
    .clk(out_12), .T(1'b1), .Q(t_ff_1_q), .reset(CLR));  // open: Qn, preset, en
  Multiplexer #(.width(8), .enable("false")) multiplexer_4 (
    .in0(\mod60计数器_1_q1a ), .in1(multiplexer_3_out),
    .out({out_6, out_7, out_8, out_9, out_10, out_11, out_13, out_14}), .sel(SET));
endmodule

module \LED电路  (
  input  AM_PM,
  input  TT,
  output [4:0] out_3,
  output [4:0] out_4,
  output [4:0] out_5,
  output [4:0] out_6
);

  wire not_1_out, not_2_out;
  wire [4:0] multiplexer_1_out, multiplexer_2_out;

  not not_1 (not_1_out, AM_PM);
  Multiplexer #(.width(5), .enable("false")) multiplexer_1 (
    .in0(5'b10000), .in1(5'b00001), .out(multiplexer_1_out), .sel(not_1_out));
  Multiplexer #(.width(5), .enable("false")) multiplexer_2 (
    .in0(5'b10100), .in1(5'b00101), .out(multiplexer_2_out), .sel(not_1_out));
  Multiplexer #(.width(5), .enable("false")) multiplexer_3 (
    .in0({5{1'b0}}), .in1(multiplexer_1_out), .out(out_3), .sel(not_2_out));
  Multiplexer #(.width(5), .enable("false")) multiplexer_4 (
    .in0({5{1'b0}}), .in1(multiplexer_2_out), .out(out_5), .sel(not_2_out));
  Multiplexer #(.width(5), .enable("false")) multiplexer_5 (
    .in0({5{1'b0}}), .in1({5{1'b1}}), .out(out_4), .sel(not_2_out));
  not not_2 (not_2_out, TT);

  assign out_6 = out_3;
endmodule

module \脉冲1HZ电路  (
  input  in_1,
  output out_2
);

  wire t_ff_1_q, t_ff_2_q;

  T_Flip_Flop t_ff_1 (.clk(in_1), .T(1'b1), .Q(t_ff_1_q));  // open: Qn, preset, reset, en
  T_Flip_Flop t_ff_2 (.clk(t_ff_1_q), .T(1'b1), .Q(t_ff_2_q));  // open: Qn, preset, reset, en
  T_Flip_Flop t_ff_3 (.clk(t_ff_2_q), .T(1'b1), .Q(out_2));  // open: Qn, preset, reset, en
endmodule

module \整点报时电路  (
  input  [3:0] in_1,
  input  [3:0] in_2,
  input  [3:0] in_3,
  input  [3:0] in_4,
  output out_5
);

  wire comparator_1_eq, comparator_2_eq, comparator_3_eq, comparator_4_eq;

  Comparator #(.width(4), .mode("unsigned")) comparator_1 (
    .a(in_1), .b(4'b0101), .eq(comparator_1_eq));  // open: gt, lt
  Comparator #(.width(4), .mode("unsigned")) comparator_2 (
    .a(in_2), .b(4'b1001), .eq(comparator_2_eq));  // open: gt, lt
  Comparator #(.width(4), .mode("unsigned")) comparator_3 (
    .a(in_3), .b(4'b0101), .eq(comparator_3_eq));  // open: gt, lt
  Comparator #(.width(1), .mode("unsigned")) comparator_4 (
    .a(in_4[0]), .b(1'b0), .eq(comparator_4_eq));  // open: gt, lt
  and and_1 (out_5, comparator_1_eq, comparator_2_eq, comparator_3_eq, comparator_4_eq);
endmodule

module \电子钟  (
  input  ADJ1,
  input  ADJ0,
  input  CPU,
  input  CLR,
  input  CP,
  input  SET,
  input  CPD,
  output \报时 ,
  output [3:0] out_9,
  output [3:0] out_10,
  output [3:0] out_11,
  output [3:0] out_12,
  output [3:0] out_13,
  output [3:0] out_14,
  output [4:0] out_15,
  output [4:0] out_16,
  output [4:0] out_17,
  output [4:0] out_18
);

  wire and_1_out, and_2_out, and_3_out, and_4_out, and_5_out, and_7_out, comparator_1_eq, comparator_2_eq,
       comparator_3_eq, \mod12_24计数器_1_out_12 , \mod60计数器_1_out_5 , \mod60计数器_2_out_5 , or_1_out, or_2_out,
       t_ff_1_q, \脉冲1hz电路_1_out_2 ;

  \脉冲1HZ电路  \u_脉冲1hz电路_1  (.in_1(CP), .out_2(\脉冲1hz电路_1_out_2 ));
  \mod60计数器  \mod60计数器_1  (
    .ADJ(1'b1), .CPU(\脉冲1hz电路_1_out_2 ), .CPD(1'b0), .Q1D(out_12[3]), .Q1C(out_12[2]), .Q1B(out_12[1]),
    .Q1A(out_12[0]), .Q2D(out_9[3]), .Q2C(out_9[2]), .Q2B(out_9[1]), .Q2A(out_9[0]),
    .out_5(\mod60计数器_1_out_5 ), .CLR(CLR));
  and and_1 (and_1_out, ADJ1, ADJ0, CPU);
  and and_2 (and_2_out, ~ADJ1, ADJ0, CPU);  // AND_Gate
  and and_3 (and_3_out, ~ADJ0, \mod60计数器_1_out_5 );  // AND_Gate
  and and_4 (and_4_out, ~ADJ1, ADJ0, CPD);  // AND_Gate
  and and_5 (and_5_out, ADJ1, ADJ0, CPD);
  or or_1 (or_1_out, and_3_out, and_2_out);
  \mod60计数器  \mod60计数器_2  (
    .ADJ(1'b1), .CPU(or_1_out), .CPD(and_4_out), .Q1D(out_13[3]), .Q1C(out_13[2]), .Q1B(out_13[1]),
    .Q1A(out_13[0]), .Q2D(out_10[3]), .Q2C(out_10[2]), .Q2B(out_10[1]), .Q2A(out_10[0]),
    .out_5(\mod60计数器_2_out_5 ), .CLR(CLR));
  Comparator #(.width(4), .mode("unsigned")) comparator_1 (
    .a(out_9), .b(4'b0101), .eq(comparator_1_eq));  // open: gt, lt
  Comparator #(.width(4), .mode("unsigned")) comparator_2 (
    .a(out_10), .b(4'b0101), .eq(comparator_2_eq));  // open: gt, lt
  Comparator #(.width(4), .mode("unsigned")) comparator_3 (
    .a(out_13), .b(4'b1001), .eq(comparator_3_eq));  // open: gt, lt
  and and_6 (\报时 , out_12[0], comparator_1_eq, comparator_2_eq, comparator_3_eq);
  and and_7 (and_7_out, ~ADJ0, \mod60计数器_2_out_5 );  // AND_Gate
  or or_2 (or_2_out, and_7_out, and_1_out);
  \mod12_24计数器  \mod12_24计数器_1  (
    .ADJ(1'b1), .CPU(or_2_out), .CPD(and_5_out), .SET(SET), .CLR(CLR), .out_6(out_11[3]), .out_7(out_11[2]),
    .out_8(out_11[1]), .out_9(out_11[0]), .out_10(out_14[3]), .out_11(out_14[2]), .out_13(out_14[1]),
    .out_14(out_14[0]), .out_12(\mod12_24计数器_1_out_12 ));
  T_Flip_Flop t_ff_1 (.clk(\mod12_24计数器_1_out_12 ), .T(1'b1), .Q(t_ff_1_q));  // open: Qn, preset, reset, en
  \LED电路  \led电路_1  (.out_3(out_15), .out_4(out_16), .out_5(out_17), .out_6(out_18), .AM_PM(t_ff_1_q), .TT(SET));
endmodule

module \闹钟  (
  input  [3:0] \hour十位 ,
  input  [3:0] \闹钟hour十位 ,
  input  [3:0] \hour个位 ,
  input  [3:0] \闹钟hour个位 ,
  input  [3:0] \minute十位 ,
  input  [3:0] \闹钟minute十位 ,
  input  [3:0] \minute个位 ,
  input  [3:0] \闹钟minute个位 ,
  input  [3:0] \second十位 ,
  input  [4:0] \上下午 ,
  input  [4:0] \闹钟上下午 ,
  output \闹钟 
);

  wire comparator_1_eq, comparator_2_eq, comparator_3_eq, comparator_4_eq, comparator_5_eq, comparator_6_eq;

  Comparator #(.width(4), .mode("unsigned")) comparator_1 (
    .a(\hour十位 ), .b(\闹钟hour十位 ), .eq(comparator_1_eq));  // open: gt, lt
  Comparator #(.width(4), .mode("unsigned")) comparator_2 (
    .a(\hour个位 ), .b(\闹钟hour个位 ), .eq(comparator_2_eq));  // open: gt, lt
  Comparator #(.width(4), .mode("unsigned")) comparator_3 (
    .a(\minute十位 ), .b(\闹钟minute十位 ), .eq(comparator_3_eq));  // open: gt, lt
  Comparator #(.width(4), .mode("unsigned")) comparator_4 (
    .a(\minute个位 ), .b(\闹钟minute个位 ), .eq(comparator_4_eq));  // open: gt, lt
  Comparator #(.width(4), .mode("unsigned")) comparator_5 (
    .a(\second十位 ), .b(4'b0000), .eq(comparator_5_eq));  // open: gt, lt
  Comparator #(.width(5), .mode("unsigned")) comparator_6 (
    .a(\上下午 ), .b(\闹钟上下午 ), .eq(comparator_6_eq));  // open: gt, lt
  and and_1 (\闹钟 , comparator_1_eq, comparator_2_eq, comparator_3_eq, comparator_4_eq, comparator_5_eq, comparator_6_eq);
endmodule

module \电子钟_闹钟  (
  input  ADJ0,
  input  ALARM,
  input  ADJ1,
  input  in_4,
  input  in_5,
  input  in_6,
  input  in_7,
  input  CLR,
  output \报时 ,
  output [3:0] out_10,
  output [3:0] out_11,
  output [3:0] out_12,
  output [3:0] out_13,
  output \报时_2 ,
  output [3:0] out_15,
  output [3:0] out_16,
  output [4:0] out_17,
  output [4:0] out_18,
  output [4:0] out_19,
  output [4:0] out_20
);

  wire and_2_out, and_3_out, and_4_out, and_5_out, and_6_out, and_7_out, and_8_out, and_9_out, and_10_out,
       and_11_out, \电子钟_1_报时 ;
  wire [3:0] \电子钟_1_out_9 , \电子钟_1_out_10 , \电子钟_1_out_11 , \电子钟_1_out_12 , \电子钟_1_out_13 , \电子钟_1_out_14 ,
       \电子钟_2_out_9 , \电子钟_2_out_10 , \电子钟_2_out_11 , \电子钟_2_out_12 , \电子钟_2_out_13 , \电子钟_2_out_14 ;
  wire [4:0] \电子钟_1_out_15 , \电子钟_1_out_16 , \电子钟_1_out_17 , \电子钟_1_out_18 , \电子钟_2_out_15 , \电子钟_2_out_16 ,
       \电子钟_2_out_17 , \电子钟_2_out_18 ;

  // AND_Gate and_1 has open pins: in0=in_4, in1=ALARM, out=open
  and and_2 (and_2_out, in_4, ~ALARM);  // AND_Gate
  and and_3 (and_3_out, in_5, ALARM);
  and and_4 (and_4_out, in_5, ~ALARM);  // AND_Gate
  and and_5 (and_5_out, in_6, ALARM);
  and and_6 (and_6_out, in_6, ~ALARM);  // AND_Gate
  and and_7 (and_7_out, CLR, ALARM);
  and and_8 (and_8_out, CLR, ~ALARM);  // AND_Gate
  and and_9 (and_9_out, ALARM, ADJ1);
  and and_10 (and_10_out, ADJ0, ~ALARM);  // AND_Gate
  and and_11 (and_11_out, ADJ1, ~ALARM);  // AND_Gate
  \电子钟  \u_电子钟_1  (
    .CP(and_2_out), .ADJ0(and_10_out), .ADJ1(and_11_out), .CPU(and_4_out), .CPD(and_6_out), .CLR(and_8_out),
    .SET(in_7), .\报时 (\电子钟_1_报时 ), .out_9(\电子钟_1_out_9 ), .out_12(\电子钟_1_out_12 ), .out_10(\电子钟_1_out_10 ),
    .out_13(\电子钟_1_out_13 ), .out_11(\电子钟_1_out_11 ), .out_14(\电子钟_1_out_14 ), .out_15(\电子钟_1_out_15 ),
    .out_16(\电子钟_1_out_16 ), .out_17(\电子钟_1_out_17 ), .out_18(\电子钟_1_out_18 ));
  and and_12 (\报时_2 , \电子钟_1_报时 , ~ALARM);  // AND_Gate
  \电子钟  \u_电子钟_2  (
    .ADJ0(1'b1), .ADJ1(and_9_out), .CPU(and_3_out), .CPD(and_5_out), .CLR(and_7_out), .SET(in_7),
    .out_9(\电子钟_2_out_9 ), .out_12(\电子钟_2_out_12 ), .out_10(\电子钟_2_out_10 ), .out_13(\电子钟_2_out_13 ),
    .out_11(\电子钟_2_out_11 ), .out_14(\电子钟_2_out_14 ), .out_15(\电子钟_2_out_15 ), .out_16(\电子钟_2_out_16 ),
    .out_17(\电子钟_2_out_17 ), .out_18(\电子钟_2_out_18 ));  // open: CP, 报时
  \闹钟  \u_闹钟_1  (
    .\hour十位 (\电子钟_1_out_11 ), .\闹钟hour十位 (\电子钟_2_out_11 ), .\hour个位 (\电子钟_1_out_14 ),
    .\闹钟hour个位 (\电子钟_2_out_14 ), .\minute十位 (\电子钟_1_out_10 ), .\闹钟minute十位 (\电子钟_2_out_10 ),
    .\minute个位 (\电子钟_1_out_13 ), .\闹钟minute个位 (\电子钟_2_out_13 ), .\second十位 (\电子钟_1_out_9 ),
    .\上下午 (\电子钟_1_out_15 ), .\闹钟上下午 (\电子钟_2_out_15 ), .\闹钟 (\报时 ));
  Multiplexer #(.width(5), .enable("false")) multiplexer_1 (
    .in0(\电子钟_1_out_15 ), .in1(\电子钟_2_out_15 ), .out(out_17), .sel(ALARM));
  Multiplexer #(.width(5), .enable("false")) multiplexer_2 (
    .in0(\电子钟_1_out_16 ), .in1(\电子钟_2_out_16 ), .out(out_18), .sel(ALARM));
  Multiplexer #(.width(5), .enable("false")) multiplexer_3 (
    .in0(\电子钟_1_out_17 ), .in1(\电子钟_2_out_17 ), .out(out_19), .sel(ALARM));
  Multiplexer #(.width(5), .enable("false")) multiplexer_4 (
    .in0(\电子钟_1_out_18 ), .in1(\电子钟_2_out_18 ), .out(out_20), .sel(ALARM));
  Multiplexer #(.width(4), .enable("false")) multiplexer_5 (
    .in0(\电子钟_1_out_11 ), .in1(\电子钟_2_out_11 ), .out(out_10), .sel(ALARM));
  Multiplexer #(.width(4), .enable("false")) multiplexer_6 (
    .in0(\电子钟_1_out_14 ), .in1(\电子钟_2_out_14 ), .out(out_11), .sel(ALARM));
  Multiplexer #(.width(4), .enable("false")) multiplexer_7 (
    .in0(\电子钟_1_out_10 ), .in1(\电子钟_2_out_10 ), .out(out_12), .sel(ALARM));
  Multiplexer #(.width(4), .enable("false")) multiplexer_8 (
    .in0(\电子钟_1_out_13 ), .in1(\电子钟_2_out_13 ), .out(out_13), .sel(ALARM));
  Multiplexer #(.width(4), .enable("false")) multiplexer_9 (
    .in0(\电子钟_1_out_9 ), .in1(\电子钟_2_out_9 ), .out(out_15), .sel(ALARM));
  Multiplexer #(.width(4), .enable("false")) multiplexer_10 (
    .in0(\电子钟_1_out_12 ), .in1(\电子钟_2_out_12 ), .out(out_16), .sel(ALARM));
endmodule

module CESHI (
  input  in_1,
  input  in_2,
  input  in_3,
  input  in_4,
  input  in_5,
  input  [3:0] in_6,
  input  [3:0] in_7,
  input  in_8,
  input  in_9,
  input  [3:0] in_10,
  input  in_11,
  input  in_12,
  input  in_13,
  input  [3:0] in_14,
  input  [3:0] in_15,
  input  [3:0] in_16,
  input  [3:0] in_17,
  input  [3:0] in_18,
  input  [3:0] in_19,
  input  [3:0] in_20,
  input  [3:0] in_21,
  input  [3:0] in_22,
  input  [4:0] in_23,
  input  [4:0] in_24,
  input  in_25,
  input  in_26,
  output out_27,
  output out_28,
  output out_29
);

  wire button_1_out, button_2_out, button_3_out, button_4_out, button_5_out, button_6_out, clock_1_out,
       clock_2_out, \整点报时电路_1_out_5 , \电子钟_闹钟_1_报时 , \电子钟_闹钟_1_报时_2 , \闹钟_1_闹钟 ;
  wire [3:0] \mod12_24计数器_1_out_9 , \mod12_24计数器_1_out_14 , \mod60计数器_1_q1a , \mod60计数器_1_q2a ,
       \电子钟_闹钟_1_out_10 , \电子钟_闹钟_1_out_11 , \电子钟_闹钟_1_out_12 , \电子钟_闹钟_1_out_13 , \电子钟_闹钟_1_out_15 ,
       \电子钟_闹钟_1_out_16 ;
  wire [4:0] \led电路_1_out_3 , \led电路_1_out_4 , \led电路_1_out_5 , \led电路_1_out_6 , \电子钟_闹钟_1_out_17 ,
       \电子钟_闹钟_1_out_18 , \电子钟_闹钟_1_out_19 , \电子钟_闹钟_1_out_20 ;

  DotMatrix #(.matrixcols(4), .matrixrows(5)) dotmatrix_1 (
    .col0(\led电路_1_out_3 ), .col1(\led电路_1_out_4 ), .col2(\led电路_1_out_5 ), .col3(\led电路_1_out_6 ));
  \LED电路  \led电路_1  (
    .out_3(\led电路_1_out_3 ), .out_4(\led电路_1_out_4 ), .out_5(\led电路_1_out_5 ), .out_6(\led电路_1_out_6 ),
    .AM_PM(in_12), .TT(in_13));
  DotMatrix #(.matrixcols(4), .matrixrows(5)) dotmatrix_2 (
    .col0(\电子钟_闹钟_1_out_17 ), .col1(\电子钟_闹钟_1_out_18 ), .col2(\电子钟_闹钟_1_out_19 ), .col3(\电子钟_闹钟_1_out_20 ));
  Clock clock_1 (.out(clock_1_out));
  Clock clock_2 (.out(clock_2_out));
  Hex_Digit_Display hex_digit_display_1 (.value(\电子钟_闹钟_1_out_10 ));  // open: dp
  Button button_1 (.out(button_1_out));
  \整点报时电路  \u_整点报时电路_1  (.in_1(in_6), .in_2(in_7), .in_3(in_10), .out_5(\整点报时电路_1_out_5 ));  // open: in_4
  \脉冲1HZ电路  \u_脉冲1hz电路_1  (.in_1(clock_2_out), .out_2(out_28));
  Hex_Digit_Display hex_digit_display_2 (.value(\电子钟_闹钟_1_out_11 ));  // open: dp
  Hex_Digit_Display hex_digit_display_3 (.value(\电子钟_闹钟_1_out_12 ));  // open: dp
  \电子钟_闹钟  \u_电子钟_闹钟_1  (
    .ADJ0(in_1), .ALARM(in_3), .ADJ1(in_2), .in_4(clock_1_out), .in_5(button_1_out), .in_6(button_2_out),
    .in_7(in_4), .CLR(in_5), .out_10(\电子钟_闹钟_1_out_10 ), .out_11(\电子钟_闹钟_1_out_11 ),
    .out_12(\电子钟_闹钟_1_out_12 ), .out_13(\电子钟_闹钟_1_out_13 ), .\报时_2 (\电子钟_闹钟_1_报时_2 ),
    .out_15(\电子钟_闹钟_1_out_15 ), .out_16(\电子钟_闹钟_1_out_16 ), .out_17(\电子钟_闹钟_1_out_17 ),
    .out_18(\电子钟_闹钟_1_out_18 ), .out_19(\电子钟_闹钟_1_out_19 ), .out_20(\电子钟_闹钟_1_out_20 ), .\报时 (\电子钟_闹钟_1_报时 ));
  Button button_2 (.out(button_2_out));
  LED led_1 (.in(\整点报时电路_1_out_5 ));
  \闹钟  \u_闹钟_1  (
    .\hour十位 (in_14), .\闹钟hour十位 (in_15), .\hour个位 (in_16), .\闹钟hour个位 (in_17), .\minute十位 (in_18),
    .\闹钟minute十位 (in_19), .\minute个位 (in_20), .\闹钟minute个位 (in_21), .\second十位 (in_22), .\上下午 (in_23),
    .\闹钟上下午 (in_24), .\闹钟 (\闹钟_1_闹钟 ));
  Hex_Digit_Display hex_digit_display_4 (.value(\电子钟_闹钟_1_out_13 ));  // open: dp
  LED led_2 (.in(\闹钟_1_闹钟 ));
  Hex_Digit_Display hex_digit_display_5 (.value(\电子钟_闹钟_1_out_15 ));  // open: dp
  Hex_Digit_Display hex_digit_display_6 (.value(\电子钟_闹钟_1_out_16 ));  // open: dp
  LED led_3 (.in(\电子钟_闹钟_1_报时 ));
  LED led_4 (.in(\电子钟_闹钟_1_报时_2 ));
  Button button_3 (.out(button_3_out));
  Button button_4 (.out(button_4_out));
  Button button_5 (.out(button_5_out));
  Button button_6 (.out(button_6_out));
  Hex_Digit_Display hex_digit_display_7 (.value(\mod12_24计数器_1_out_9 ));  // open: dp
  \mod12_24计数器  \mod12_24计数器_1  (
    .ADJ(in_8), .CPU(button_3_out), .CPD(button_4_out), .SET(in_9), .CLR(in_11),
    .out_6(\mod12_24计数器_1_out_9 [3]), .out_7(\mod12_24计数器_1_out_9 [2]), .out_8(\mod12_24计数器_1_out_9 [1]),
    .out_9(\mod12_24计数器_1_out_9 [0]), .out_10(\mod12_24计数器_1_out_14 [3]), .out_11(\mod12_24计数器_1_out_14 [2]),
    .out_13(\mod12_24计数器_1_out_14 [1]), .out_14(\mod12_24计数器_1_out_14 [0]), .out_12(out_27));
  Hex_Digit_Display hex_digit_display_8 (.value(\mod60计数器_1_q2a ));  // open: dp
  \mod60计数器  \mod60计数器_1  (
    .ADJ(in_25), .CPU(button_5_out), .CPD(button_6_out), .Q1D(\mod60计数器_1_q1a [3]),
    .Q1C(\mod60计数器_1_q1a [2]), .Q1B(\mod60计数器_1_q1a [1]), .Q1A(\mod60计数器_1_q1a [0]),
    .Q2D(\mod60计数器_1_q2a [3]), .Q2C(\mod60计数器_1_q2a [2]), .Q2B(\mod60计数器_1_q2a [1]),
    .Q2A(\mod60计数器_1_q2a [0]), .out_5(out_29), .CLR(in_26));
  Hex_Digit_Display hex_digit_display_9 (.value(\mod12_24计数器_1_out_14 ));  // open: dp
  Hex_Digit_Display hex_digit_display_10 (.value(\mod60计数器_1_q1a ));  // open: dp
endmodule

module temp (
  input  in_1,
  output out_2
);

  wire buffer_1_out, buffer_2_out, buffer_3_out, buffer_4_out, buffer_5_out, buffer_6_out, buffer_7_out,
       buffer_8_out;

  buf buffer_1 (buffer_1_out, buffer_2_out);
  buf buffer_2 (buffer_2_out, in_1);
  buf buffer_3 (buffer_3_out, buffer_4_out);
  buf buffer_4 (buffer_4_out, buffer_5_out);
  buf buffer_5 (buffer_5_out, buffer_1_out);
  buf buffer_6 (buffer_6_out, buffer_7_out);
  buf buffer_7 (buffer_7_out, buffer_8_out);
  buf buffer_8 (buffer_8_out, buffer_3_out);
  buf buffer_9 (out_2, buffer_6_out);
endmodule
